# Fritzing sketch contoh 1 (saved by Fritzing 0.9.10b)
breadboards: 1

parts:
  Part1 = Arduino Uno (Rev3)
  HC-SR04_Sensor_1 = HC-SR04 Ultrasonic Distance Sensor
  J1 = Basic Servo

nets:
  N1: Part1.D8, HC-SR04_Sensor_1.TRIG
  N2: Part1.D6_PWM, J1.pulse
  N3: Part1.D7, HC-SR04_Sensor_1.ECHO
  VCC: Part1.5V, HC-SR04_Sensor_1.VCC, J1.vcc
  GND: Part1.GND, HC-SR04_Sensor_1.GND, J1.gnd
